// Logisim project tmi.circ as structural Verilog: 4 circuits, main circuit main
module main (
);

  wire _0_out, button_2_out, button_out, cell_1_clk_2, cell_1_is_active_2, cell_1_set_head, cell_2_clk_2,
       cell_2_is_active, cell_2_is_active_2, cell_2_set_head, cell_2_set_tail, cell_3_clk_2,
       cell_3_is_active, cell_3_is_active_2, cell_3_set_head, cell_3_set_tail, cell_4_clk_2,
       cell_4_is_active, cell_4_is_active_2, cell_4_set_head, cell_4_set_tail, cell_5_is_active,
       cell_5_set_tail, cpu_1_clk, cpu_1_fake_act, cpu_1_next_bf_cmd, cpu_1_tty_clk, priority_encoder_1_p5,
       priority_encoder_1_p6, priority_encoder_1_p7, priority_encoder_1_p8, START_out;
  wire [2:0] cell_1_cmd_2, cell_1_dbg_led, cell_2_cmd_2, cell_2_dbg_led, cell_3_cmd_2, cell_3_dbg_led,
       cell_4_cmd_2, cell_4_dbg_led, cell_5_cmd_2, cell_5_dbg_led, CMD, cpu_1_cmd;
  wire [3:0] cell_1_dbg_mem, cell_1_dbg_mem_2, cell_2_dbg_mem, cell_2_dbg_mem_2, cell_3_dbg_mem,
       cell_3_dbg_mem_2, cell_4_dbg_mem, cell_4_dbg_mem_2, cell_5_dbg_mem, cell_5_dbg_mem_2, rom_2_data,
       tape_1_bf_cmd;
  wire [6:0] cpu_1_disp;
  wire [7:0] cell_1_data_in_2, cell_1_data_out_2, cell_2_data_in_2, cell_2_data_out_2, cell_3_data_in_2,
       cell_3_data_out_2, cell_4_data_in_2, cell_4_data_out_2, cell_5_data_out_2, cpu_1_data_to_cell;
  wire [11:0] tape_1_address;

  ROM #(.addrWidth(12), .dataWidth(4)) rom_1 ();  // open: addr, data, sel
  Hex_Digit_Display hex_digit_display_1 (.value(rom_2_data));  // open: dp
  ROM #(.addrWidth(12), .dataWidth(4)) rom_2 (.addr(tape_1_address), .data(rom_2_data));  // open: sel
  tape tape_1 (
    .ADDRESS(tape_1_address), .DATA(rom_2_data), .CLK(cpu_1_clk), .BF_NEXT(cpu_1_next_bf_cmd),
    .BF_CMD(tape_1_bf_cmd));
  TTY tty_1 (.data(cpu_1_disp), .clk(cpu_1_tty_clk));  // open: we, clr
  Button START (.out(START_out));
  cpu cpu_1 (
    .NEXT_BF_CMD(cpu_1_next_bf_cmd), .BF_CMD(tape_1_bf_cmd), .START(START_out), .DISP(cpu_1_disp),
    .TTY_CLK(cpu_1_tty_clk), .FAKE_ACT(cpu_1_fake_act), .DATA_TO_CELL(cpu_1_data_to_cell),
    .DATA_FROM_CELL(cell_1_data_out_2), .CMD(cpu_1_cmd), .CLK(cpu_1_clk));
  \cell  cell_1 (
    .IS_ACTIVE_LEFT(cpu_1_fake_act), .DATA_IN(cpu_1_data_to_cell), .DATA_OUT_2(cell_1_data_out_2),
    .CMD(cpu_1_cmd), .CLK(cpu_1_clk), .IS_TAIL(cell_2_set_tail), .SET_HEAD(cell_1_set_head),
    .IS_ACTIVE_RIGHT(cell_2_is_active), .IS_ACTIVE_2(cell_1_is_active_2), .DATA_IN_2(cell_1_data_in_2),
    .DATA_OUT(cell_2_data_out_2), .CMD_2(cell_1_cmd_2), .CLK_2(cell_1_clk_2),
    .DBG_MEM({cell_1_dbg_mem_2, cell_1_dbg_mem}), .DBG_LED(cell_1_dbg_led));  // open: SET_TAIL, IS_HEAD, IS_ACTIVE
  DotMatrix #(.matrixcols(3), .matrixrows(1)) dotmatrix_1 (
    .col0(cell_1_dbg_led[0]), .col1(cell_1_dbg_led[1]), .col2(cell_1_dbg_led[2]));
  Hex_Digit_Display hex_digit_display_2 (.value(cell_1_dbg_mem));  // open: dp
  Hex_Digit_Display hex_digit_display_3 (.value(cell_1_dbg_mem_2));  // open: dp
  Button _0 (.out(_0_out));
  DotMatrix #(.matrixcols(3), .matrixrows(1)) dotmatrix_2 (
    .col0(cell_2_dbg_led[0]), .col1(cell_2_dbg_led[1]), .col2(cell_2_dbg_led[2]));
  Hex_Digit_Display hex_digit_display_4 (.value(cell_2_dbg_mem_2));  // open: dp
  Button button (.out(button_out));
  Button button_2 (.out(button_2_out));
  // Priority_Encoder priority_encoder_1: pin names not known; wires that end beside it: _0_out, button_2_out, button_out, CMD, priority_encoder_1_p5, priority_encoder_1_p6, priority_encoder_1_p7, priority_encoder_1_p8
  \cell  cell_2 (
    .SET_TAIL(cell_2_set_tail), .IS_HEAD(cell_1_set_head), .IS_ACTIVE(cell_2_is_active),
    .IS_ACTIVE_LEFT(cell_1_is_active_2), .DATA_IN(cell_1_data_in_2), .DATA_OUT_2(cell_2_data_out_2),
    .CMD(cell_1_cmd_2), .CLK(cell_1_clk_2), .IS_TAIL(cell_3_set_tail), .SET_HEAD(cell_2_set_head),
    .IS_ACTIVE_RIGHT(cell_3_is_active), .IS_ACTIVE_2(cell_2_is_active_2), .DATA_IN_2(cell_2_data_in_2),
    .DATA_OUT(cell_3_data_out_2), .CMD_2(cell_2_cmd_2), .CLK_2(cell_2_clk_2),
    .DBG_MEM({cell_2_dbg_mem_2, cell_2_dbg_mem}), .DBG_LED(cell_2_dbg_led));
  Hex_Digit_Display hex_digit_display_5 (.value(cell_2_dbg_mem));  // open: dp
  Button button_3 (.out(priority_encoder_1_p7));
  Button R (.out(priority_encoder_1_p5));
  Button W (.out(priority_encoder_1_p6));
  \cell  cell_3 (
    .SET_TAIL(cell_3_set_tail), .IS_HEAD(cell_2_set_head), .IS_ACTIVE(cell_3_is_active),
    .IS_ACTIVE_LEFT(cell_2_is_active_2), .DATA_IN(cell_2_data_in_2), .DATA_OUT_2(cell_3_data_out_2),
    .CMD(cell_2_cmd_2), .CLK(cell_2_clk_2), .IS_TAIL(cell_4_set_tail), .SET_HEAD(cell_3_set_head),
    .IS_ACTIVE_RIGHT(cell_4_is_active), .IS_ACTIVE_2(cell_3_is_active_2), .DATA_IN_2(cell_3_data_in_2),
    .DATA_OUT(cell_4_data_out_2), .CMD_2(cell_3_cmd_2), .CLK_2(cell_3_clk_2),
    .DBG_MEM({cell_3_dbg_mem_2, cell_3_dbg_mem}), .DBG_LED(cell_3_dbg_led));
  DotMatrix #(.matrixcols(3), .matrixrows(1)) dotmatrix_3 (
    .col0(cell_3_dbg_led[0]), .col1(cell_3_dbg_led[1]), .col2(cell_3_dbg_led[2]));
  Hex_Digit_Display hex_digit_display_6 (.value(cell_3_dbg_mem_2));  // open: dp
  Hex_Digit_Display hex_digit_display_7 (.value(cell_3_dbg_mem));  // open: dp
  Button button_4 (.out(priority_encoder_1_p8));
  Hex_Digit_Display hex_digit_display_8 (.value({1'b0, CMD}));  // open: dp
  DotMatrix #(.matrixcols(3), .matrixrows(1)) dotmatrix_4 (
    .col0(cell_4_dbg_led[0]), .col1(cell_4_dbg_led[1]), .col2(cell_4_dbg_led[2]));
  Hex_Digit_Display hex_digit_display_9 (.value(cell_4_dbg_mem_2));  // open: dp
  \cell  cell_4 (
    .SET_TAIL(cell_4_set_tail), .IS_HEAD(cell_3_set_head), .IS_ACTIVE(cell_4_is_active),
    .IS_ACTIVE_LEFT(cell_3_is_active_2), .DATA_IN(cell_3_data_in_2), .DATA_OUT_2(cell_4_data_out_2),
    .CMD(cell_3_cmd_2), .CLK(cell_3_clk_2), .IS_TAIL(cell_5_set_tail), .SET_HEAD(cell_4_set_head),
    .IS_ACTIVE_RIGHT(cell_5_is_active), .IS_ACTIVE_2(cell_4_is_active_2), .DATA_IN_2(cell_4_data_in_2),
    .DATA_OUT(cell_5_data_out_2), .CMD_2(cell_4_cmd_2), .CLK_2(cell_4_clk_2),
    .DBG_MEM({cell_4_dbg_mem_2, cell_4_dbg_mem}), .DBG_LED(cell_4_dbg_led));
  Hex_Digit_Display hex_digit_display_10 (.value(cell_4_dbg_mem));  // open: dp
  \cell  cell_5 (
    .SET_TAIL(cell_5_set_tail), .IS_HEAD(cell_4_set_head), .IS_ACTIVE(cell_5_is_active),
    .IS_ACTIVE_LEFT(cell_4_is_active_2), .DATA_IN(cell_4_data_in_2), .DATA_OUT_2(cell_5_data_out_2),
    .CMD(cell_4_cmd_2), .CLK(cell_4_clk_2), .CMD_2(cell_5_cmd_2),
    .DBG_MEM({cell_5_dbg_mem_2, cell_5_dbg_mem}), .DBG_LED(cell_5_dbg_led));  // open: IS_TAIL, SET_HEAD, IS_ACTIVE_RIGHT, IS_ACTIVE_2, DATA_IN_2, DATA_OUT, CLK_2
  DotMatrix #(.matrixcols(3), .matrixrows(1)) dotmatrix_5 (
    .col0(cell_5_dbg_led[0]), .col1(cell_5_dbg_led[1]), .col2(cell_5_dbg_led[2]));
  Hex_Digit_Display hex_digit_display_11 (.value(cell_5_dbg_mem));  // open: dp
  Hex_Digit_Display hex_digit_display_12 (.value(cell_5_dbg_mem_2));  // open: dp
  Hex_Digit_Display hex_digit_display_13 (.value({1'b0, cell_5_cmd_2}));  // open: dp

  // Notes on the sheet:
  //   [Hello, world]
  //   Hello, world
  //   contents of rom_1 (hex, n*v repeats v):
  //   10*6 1 3 7*6 3 10*6 3 6 6 6 3 6 4*2 7 0 3 6 6 4 3 6 4 7*6 4 4 6 6 6 4 3 6 6 4 2 2 15*6 4 3 4 6 6 6 4
  //   6*7 4 8*7 4 3 6 4 3 4 8
  //   contents of rom_2 (hex, n*v repeats v):
  //   72*6 4 29*6 4 7*6 4 4 6 6 6 4 79*7 4 55*6 4 24*6 4 6 6 6 4 6*7 4 8*7 4 67*7 4 23*7 4 8
endmodule

// memcell
module \cell  (
  input  IS_TAIL,
  input  IS_HEAD,
  input  IS_ACTIVE_RIGHT,
  input  IS_ACTIVE_LEFT,
  input  [7:0] DATA_IN,
  input  [7:0] DATA_OUT,
  input  [2:0] CMD,
  input  CLK,
  output SET_TAIL,
  output SET_HEAD,
  output IS_ACTIVE,
  output [7:0] DBG_MEM,
  output [2:0] DBG_LED,
  output IS_ACTIVE_2,
  output [7:0] DATA_IN_2,
  output [7:0] DATA_OUT_2,
  output [2:0] CMD_2,
  output CLK_2
);

  wire and_1_out, and_5_out, and_6_out, bitselector_1_out, bitselector_2_out, COUNT, decoder_1_out0, LOAD,
       minus_ACT, not_1_out, not_2_out, not_3_out, not_4_out, not_5_out, plus_1__1, plus_ACT, R_W, RST,
       s_r_ff_1_q, tunnel, WRITE;
  wire [7:0] controlled_buffer_5_out;

  Pull_Resistor #(.pull(1)) pull_resistor_1 (.node(IS_HEAD));
  Pull_Resistor pull_resistor_2 (.node(IS_ACTIVE_LEFT));
  BitSelector #(.width(2)) bitselector_1 (.in({IS_TAIL, IS_HEAD}), .out(bitselector_1_out), .sel(CMD[0]));
  BitSelector #(.width(2)) bitselector_2 (
    .in({IS_ACTIVE_LEFT, IS_ACTIVE_RIGHT}), .out(bitselector_2_out), .sel(CMD[0]));
  and and_1 (and_1_out, plus_1__1, DBG_LED[1]);
  and and_2 (WRITE, R_W, CMD[0], DBG_LED[1]);
  not not_1 (not_1_out, bitselector_1_out);
  not not_2 (not_2_out, DBG_LED[1]);
  assign LOAD = and_1_out ? CMD[0] : 1'bz;  // Controlled_Buffer controlled_buffer_1
  assign COUNT = and_1_out ? 1'b1 : 1'bz;  // Controlled_Buffer controlled_buffer_2
  assign LOAD = WRITE ? 1'b1 : 1'bz;  // Controlled_Buffer controlled_buffer_3
  assign COUNT = WRITE ? 1'b0 : 1'bz;  // Controlled_Buffer controlled_buffer_4
  Pull_Resistor pull_resistor_3 (.node(DATA_IN));
  Pull_Resistor pull_resistor_4 (.node(CMD));
  Pull_Resistor pull_resistor_5 (.node(CLK));
  and and_3 (minus_ACT, DBG_LED[1], tunnel, not_1_out);
  and and_4 (plus_ACT, not_2_out, tunnel, bitselector_2_out);
  Pull_Resistor #(.pull(1)) pull_resistor_6 (.node(IS_TAIL));
  Pull_Resistor pull_resistor_7 (.node(IS_ACTIVE_RIGHT));
  assign controlled_buffer_5_out = WRITE ? DATA_IN : 8'bz;  // Controlled_Buffer controlled_buffer_5
  Pull_Resistor pull_resistor_8 (.node(LOAD));
  Pull_Resistor pull_resistor_9 (.node(COUNT));
  Decoder #(.select(2), .disabled(0), .enable("false")) decoder_1 (
    .out0(decoder_1_out0), .out1(tunnel), .out2(R_W), .out3(plus_1__1), .sel(CMD[2:1]));
  not not_3 (not_3_out, CLK);
  S_R_Flip_Flop s_r_ff_1 (.S(plus_ACT), .clk(CLK), .R(minus_ACT), .Q(s_r_ff_1_q), .reset(RST));  // open: Qn, preset, en
  Counter counter_1 (
    .load(LOAD), .D(controlled_buffer_5_out), .count(COUNT), .Q(DBG_MEM), .clk(CLK), .clr(RST));  // open: carry
  and and_5 (and_5_out, not_4_out, DBG_LED[1], R_W);
  not not_4 (not_4_out, CMD[0]);
  and and_6 (and_6_out, CMD[0], decoder_1_out0);
  D_Flip_Flop d_ff_1 (.clk(not_3_out), .D(s_r_ff_1_q), .Q(DBG_LED[1]), .reset(RST));  // open: Qn, preset, en
  assign DATA_OUT = and_5_out ? DBG_MEM : 8'bz;  // Controlled_Buffer controlled_buffer_6
  D_Flip_Flop d_ff_2 (.clk(CLK), .D(and_6_out), .Q(RST), .reset(not_5_out));  // open: Qn, preset, en
  not not_5 (not_5_out, and_6_out);

  assign CLK_2 = CLK;
  assign CMD_2 = CMD;
  assign DATA_IN_2 = DATA_IN;
  assign DATA_OUT_2 = DATA_OUT;
  assign {DBG_LED[2], DBG_LED[0]} = {IS_TAIL, IS_HEAD};
  assign IS_ACTIVE = DBG_LED[1];
  assign IS_ACTIVE_2 = DBG_LED[1];
  assign SET_HEAD = 1'b0;
  assign SET_TAIL = 1'b0;

  // Other names for the same wires on the sheet: AR = IS_ACTIVE_RIGHT; AL = IS_ACTIVE_LEFT; HEAD = IS_HEAD;
  //   ACT = DBG_LED[1]; TAIL = IS_TAIL; IN[7:0] = DATA_IN; OUT[7:0] = DATA_OUT
endmodule

module cpu (
  input  START,
  input  [7:0] DATA_FROM_CELL,
  input  [3:0] BF_CMD,
  output TTY_CLK,
  output [6:0] DISP,
  output FAKE_ACT,
  output NEXT_BF_CMD,
  output [7:0] DATA_TO_CELL,
  output [2:0] CMD,
  output CLK
);

  wire and_1_out, and_2_out, buffer_2_out, CLK_t, d_ff_1_q, d_ff_3_q, IN, INIT1, INIT2, INIT3, INIT4, INIT5,
       not_2_out, not_3_out, not_4_out, pull_resistor_3_node, SEND;
  wire [2:0] controlled_buffer_1_out, counter_1_q;
  wire [7:7] DISP_t;

  Clock clock_1 (.out(CLK_t));
  D_Flip_Flop d_ff_1 (.Q(d_ff_1_q), .preset(START), .reset(NEXT_BF_CMD));  // open: clk, D, Qn, en
  and and_1 (and_1_out, d_ff_1_q, CLK_t);
  Pull_Resistor pull_resistor_1 (.node(BF_CMD[2:0]));
  Pull_Resistor #(.pull(1)) pull_resistor_2 (.node(BF_CMD[3]));
  Counter #(.width(3), .max('h7)) counter_1 (
    .count(and_1_out), .Q(counter_1_q), .clk(and_1_out));  // open: load, D, carry, clr
  not not_1 (SEND, BF_CMD[3]);
  assign controlled_buffer_1_out = INIT1 ? 3'b001 : 3'bz;  // Controlled_Buffer controlled_buffer_1
  nor nor_1 (IN, BF_CMD[0], BF_CMD[1], not_2_out);
  not not_2 (not_2_out, BF_CMD[2]);
  assign controlled_buffer_1_out = INIT5 ? 3'b000 : 3'bz;  // Controlled_Buffer controlled_buffer_2
  Decoder #(.select(3), .enable("false")) decoder_1 (
    .out1(INIT1), .out2(INIT2), .out3(INIT3), .out4(INIT4), .out5(INIT5), .out6(NEXT_BF_CMD),
    .sel(counter_1_q));  // open: out0, out7
  assign controlled_buffer_1_out = INIT3 ? 3'b011 : 3'bz;  // Controlled_Buffer controlled_buffer_3
  assign controlled_buffer_1_out = SEND ? BF_CMD[2:0] : 3'bz;  // Controlled_Buffer controlled_buffer_4
  not not_3 (not_3_out, CLK_t);
  D_Flip_Flop d_ff_2 (.Q(FAKE_ACT), .preset(INIT3), .reset(INIT5));  // open: clk, D, Qn, en
  D_Flip_Flop d_ff_3 (.Q(d_ff_3_q), .preset(IN));  // open: clk, D, Qn, en, reset
  Register #(.width(3)) register_1 (.D(controlled_buffer_1_out), .Q(CMD), .clk(not_3_out));  // open: en, clr
  assign {DISP_t[7], DISP} = d_ff_3_q ? DATA_FROM_CELL : 8'bz;  // Controlled_Buffer controlled_buffer_5
  and and_2 (and_2_out, NEXT_BF_CMD, CLK_t);
  Hex_Digit_Display hex_digit_display_1 (.value({1'b0, CMD}));  // open: dp
  or or_1 (CLK, INIT2, and_2_out, INIT4);
  or or_2 (TTY_CLK, pull_resistor_3_node, not_4_out);
  Pull_Resistor pull_resistor_3 (.node(pull_resistor_3_node));
  not not_4 (not_4_out, buffer_2_out);
  buf buffer_1 (pull_resistor_3_node, DISP_t[7]);
  buf buffer_2 (buffer_2_out, DISP_t[7]);
  Pull_Resistor #(.pull(1)) pull_resistor_4 (.node(buffer_2_out));

  // Other names for the same wires on the sheet: SEND_CMD[2:0] = BF_CMD[2:0]; DISP_t[6:0] = DISP; RDY = NEXT_BF_CMD
endmodule

module tape (
  input  BF_NEXT,
  input  CLK,
  input  [3:0] DATA,
  output [11:0] ADDRESS,
  output [3:0] BF_CMD
);

  wire and_1_out, and_2_out, not_1_out;

  and and_1 (and_1_out, BF_NEXT, not_1_out);
  not not_1 (not_1_out, CLK);
  Counter #(.width(12), .max('hfff)) counter_1 (
    .count(and_1_out), .Q(ADDRESS), .clk(and_1_out));  // open: load, D, carry, clr
  assign BF_CMD = and_2_out ? DATA : 4'bz;  // Controlled_Buffer controlled_buffer_1
  and and_2 (and_2_out, BF_NEXT, CLK);

  // Other names for the same wires on the sheet: NEXT = BF_NEXT
endmodule
